# Fritzing sketch engine (saved by Fritzing 0.7.5b)
breadboards: 1

parts:
  Q1 = Basic FET N-Channel [package="TO220 [THT]"]
  Arduino1 = Arduino
  K1 = Relay [part_number=FRS1B-S package=THT]
  K2 = Relay [part_number=FRS1B-S package=THT]
  Q2 = Basic FET N-Channel [package="TO220 [THT]"]
  VCC1 = 4 x AAA Battery Mount
  LED1 = LED - 5mm [color="Red (633nm)" package="5 mm [THT]"]
  R1 = Resistor [tolerance=±5% resistance=220 package=THT]
  R2 = Photocell (LDR) [package=THT]
  R3 = Resistor [tolerance=±5% resistance=1k package=THT]
  LED2 = LED - 5mm [color="Green (560nm)" package="5 mm [THT]"]
  R4 = Resistor [tolerance=±5% resistance=1k package=THT]
  M1 = DC Motor
  VCC2 = 4 x AAA Battery Mount
  VCC3 = 4 x AAA Battery Mount
  R5 = Resistor [tolerance=±5% resistance=1k package=THT]

nets:
  N1: Q1.gate, VCC1.-, R1.Pin_1, R5.Pin_1
  N2: Q1.drain, K1.COIL1, K2.COIL1
  N3: Q1.source, Arduino1.D2, R5.Pin_0
  N4: Arduino1.D3, LED1.cathode
  N5: K1.A, K2.B, M1.pin_2
  N6: K1.C1, K1.C2, R2.pin_1, R4.Pin_0, VCC3.+
  N7: K1.COIL2, K2.COIL2, VCC1.+
  N8: K1.B, K2.A, M1.pin_1
  N9: K2.C1, K2.C2, Q2.drain, LED2.cathode, LED2.anode, R4.Pin_1
  N10: Q2.gate, R3.Pin_1, VCC2.-
  N11: Q2.source, R2.pin_0, R3.Pin_0
  N12: LED1.anode, R1.Pin_0
  N13: VCC2.+, VCC3.-
